// Logisim project 4-bit input loader.circ as structural Verilog: 1 circuit, main circuit main
module main (
  input  Load,
  input  I1,
  input  I2,
  input  I3,
  input  I4,
  output out_6,
  output out_7,
  output out_8,
  output out_9
);

  D_Flip_Flop d_ff_1 (.clk(Load), .D(I1), .Q(out_6));  // open: Qn, preset, en, reset
  D_Flip_Flop d_ff_2 (.clk(Load), .D(I2), .Q(out_7));  // open: Qn, preset, en, reset
  D_Flip_Flop d_ff_3 (.clk(Load), .D(I3), .Q(out_8));  // open: Qn, preset, en, reset
  D_Flip_Flop d_ff_4 (.clk(Load), .D(I4), .Q(out_9));  // open: Qn, preset, en, reset
endmodule
